# Fritzing sketch TeenAstroHandV1.2 (saved by Fritzing 0.9.3b)
circuit board: 5.49999cm x 9.00001cm
breadboards: 1

parts:
  North = screw terminal, 2 pins
  East = screw terminal, 2 pins
  West = screw terminal, 2 pins
  Sud = screw terminal, 2 pins
  Fm = screw terminal, 2 pins
  Fp = screw terminal, 2 pins
  WeMos_D1_Mini2 = WeMos D1 Mini
  3V3_GND_SCL_SDA_RST = female pin header, 5 pins [form="♀ (female)"]
  C9 = Ceramic Capacitor [capacitance=100nF voltage=35V package="200 mil [THT, multilayer]"]
  C10 = Ceramic Capacitor [capacitance=100nF voltage=35V package="200 mil [THT, multilayer]"]
  C12 = Ceramic Capacitor [capacitance=100nF voltage=35V package="200 mil [THT, multilayer]"]
  C11 = Ceramic Capacitor [capacitance=100nF voltage=35V package="200 mil [THT, multilayer]"]
  C14 = Ceramic Capacitor [capacitance=100nF voltage=35V package="200 mil [THT, multilayer]"]
  C8 = Ceramic Capacitor [capacitance=100nF voltage=35V package="200 mil [THT, multilayer]"]
  C13 = Ceramic Capacitor [capacitance=100nF voltage=35V package="200 mil [THT, multilayer]"]
  Shift = screw terminal, 2 pins
  R1 = Resistor [tolerance=±5% resistance=220 power=0.25 package="2512 [SMD]"]
  R2 = Resistor [tolerance=±5% resistance=220 power=0.25 package="2512 [SMD]"]
  R13 = Resistor [tolerance=±5% resistance=220 power=0.25 package="2512 [SMD]"]
  R14 = Resistor [tolerance=±5% resistance=220 power=0.25 package="2512 [SMD]"]
  R12 = Resistor [tolerance=±5% resistance=220 power=0.25 package="2512 [SMD]"]
  R11 = Resistor [tolerance=±5% resistance=220 power=0.25 package="2512 [SMD]"]
  R10 = Resistor [tolerance=±5% resistance=220 power=0.25 package="2512 [SMD]"]
  R9 = Resistor [tolerance=±5% resistance=220 power=0.25 package="2512 [SMD]"]
  R8 = Resistor [tolerance=±5% resistance=220 power=0.25 package="2512 [SMD]"]
  RX2 = Pad [width=2.5 height=5 connect=center]
  TX2 = Pad [width=2.5 height=5 connect=center]
  TX = Pad [width=2.5 height=5 connect=center]
  RX = Pad [width=2.5 height=5 connect=center]
  GND = Pad [width=2.5 height=5 connect=center]
  5V = Pad [width=2.5 height=5 connect=center]
  SOCKET = female pin header, 6 pins [form="♀ (female)"]

nets:
  3v3: North.pin1, East.pin1, West.pin1, Sud.pin1, WeMos_D1_Mini2.3V3, 3V3_GND_SCL_SDA_RST.pin5, Shift.pin1, R2.Pin_1, R9.Pin_0, R8.Pin_0
  North: North.pin2, WeMos_D1_Mini2.D7, C12.0, R13.Pin_1
  East: East.pin2, WeMos_D1_Mini2.D0, C9.0, R10.Pin_1
  West: West.pin2, WeMos_D1_Mini2.D5, C11.0, R11.Pin_1
  Sud: Sud.pin2, WeMos_D1_Mini2.D6, C8.0, R12.Pin_1
  GND: Fm.pin1, Fp.pin1, WeMos_D1_Mini2.G, 3V3_GND_SCL_SDA_RST.pin4, C9.1, C10.1, C12.1, C11.1, C14.1, C8.1, C13.1, R1.Pin_1, R13.Pin_0, R14.Pin_0, R12.Pin_0, R11.Pin_0, R10.Pin_0, GND.pad, SOCKET.pin5
  fm: Fm.pin2, WeMos_D1_Mini2.D4, C13.0, R8.Pin_1
  fp: Fp.pin2, WeMos_D1_Mini2.D3, C10.0, R9.Pin_1
  5V: WeMos_D1_Mini2.5V, 5V.pad, SOCKET.pin6
  A0: WeMos_D1_Mini2.A0, R1.Pin_0, R2.Pin_0
  SDA: WeMos_D1_Mini2.D1, 3V3_GND_SCL_SDA_RST.pin3
  SCL: WeMos_D1_Mini2.D2, 3V3_GND_SCL_SDA_RST.pin2
  Shift: WeMos_D1_Mini2.D8, C14.0, Shift.pin2, R14.Pin_1
  RST: WeMos_D1_Mini2.RST, 3V3_GND_SCL_SDA_RST.pin1
  RX: WeMos_D1_Mini2.RX, RX.pad, SOCKET.pin1
  TX: WeMos_D1_Mini2.TX, TX.pad, SOCKET.pin2
  N1: RX2.pad, SOCKET.pin3
  N2: TX2.pad, SOCKET.pin4

notes:
  TeenAstro SHC 1.2
  SHC GPS
